# Fritzing sketch led-nodemcu (saved by Fritzing 0.9.3b)
breadboards: 1

parts:
  U2 = NodeMCU V1.0
  LED1 = LED - 3mm [color="Green (560nm)" package="3 mm [THT]"]
  LED2 = LED - 3mm [color="Yellow (595nm)" package="3 mm [THT]"]

nets:
  N1: U2.GND, LED1.anode, LED2.anode
  N2: U2.D7, LED1.cathode
  N3: U2.D8, LED2.cathode

custom parts:
  NodeMCU V1.0: ESP8266 based NodeMCU
